# Fritzing sketch wurdklok (saved by Fritzing 0.8.7b)
circuit board: 8.46667cm x 5.64444cm
breadboards: 1

parts:
  Part1 = Arduino Pro Mini v13
  JP1 = HC-05 Bluetooth Module
  C1 = Capacitor [package=cap-pth-small-kit]
  U1 = 74HC595 [package="DIP16 [THT]"]  # not connected

nets:
  GND: Part1.GND, JP1.GND, C1.2
  VCC: Part1.VCC, JP1.VCC, C1.1
